# Fritzing sketch diagram (saved by Fritzing 0.9.4)
breadboards: 2

parts:
  Part1 = Arduino Nano (Rev3.0)
  DFRobot_DFPlayer_Mini1 = DFRobot DFPlayer Mini [part_number=DFR0299]
  part = Resistor [tolerance=±5% resistance=1k package="0805 [SMD]"]
  J1 = Piezo Speaker
  S1 = Toggle Switch [package=THT]
  R2 = Resistor [tolerance=±5% resistance=10k package="0805 [SMD]"]
  LED1 = LED - 5mm [color="Yellow (595nm)" package="5 mm [THT]"]
  LED3 = LED - 5mm [color="Yellow (595nm)" package="5 mm [THT]"]
  LED2 = LED - 5mm [color="Yellow (595nm)" package="5 mm [THT]"]
  R3 = Resistor [tolerance=±5% resistance=220 package="0805 [SMD]"]
  R4 = Resistor [tolerance=±5% resistance=220 package="0805 [SMD]"]
  VCC1 = Battery block 9V
  LED4 = LED - 3mm [color="Red (660nm)" package="3 mm [THT]"]
  R6 = Resistor [tolerance=±5% resistance=220 package="0805 [SMD]"]
  R7 = Resistor [tolerance=±5% resistance=220 package="0805 [SMD]"]
  S2 = Tilt Switch [package=THT]
  R8 = Resistor [tolerance=±5% resistance=10k package="0805 [SMD]"]

nets:
  N1: Part1.D1/TX, part.Pin_1
  N2: Part1.D0/RX, DFRobot_DFPlayer_Mini1.TX
  N3: Part1.GND, DFRobot_DFPlayer_Mini1.GND-1, DFRobot_DFPlayer_Mini1.GND-2, R2.Pin_1, VCC1.-, R7.Pin_0
  N4: Part1.D9, S2.Pin_1, R8.Pin_0
  N5: Part1.D11/MOSI, R4.Pin_0
  N6: Part1.D12/MISO, R3.Pin_0
  N7: Part1.VIN, VCC1.+
  N8: Part1.D13/SCK, R6.Pin_0
  N9: DFRobot_DFPlayer_Mini1.VCC, S1.L1
  N10: DFRobot_DFPlayer_Mini1.RX, part.Pin_0
  N11: DFRobot_DFPlayer_Mini1.SPK_1, J1.pin1
  N12: DFRobot_DFPlayer_Mini1.SPK_2, J1.pin2
  N13: S1.L2, R2.Pin_0
  N14: LED1.cathode, LED3.cathode, LED2.cathode, LED4.cathode, S2.Pin_2
  N15: LED1.anode, R4.Pin_1
  N16: LED3.anode, R3.Pin_1
  N17: LED2.anode, R7.Pin_1
  N18: LED4.anode, R6.Pin_1
